# Fritzing sketch LedStripDriverWithTrimmers (saved by Fritzing 0.9.3b)
breadboards: 1

parts:
  Power_plug1 = Power plug
  Q1 = Basic FET N-Channel [part_number=IRFZ44N package="TO220 [THT]"]
  Q2 = NPN-Transistor [part_number=2N3904 package="TO92 [THT]"]
  R1 = Resistor [tolerance=±1% resistance=10k package=THT]
  R2 = Resistor [tolerance=±1% resistance=10k package=THT]
  R3 = Resistor [tolerance=±1% resistance=10k package=THT]
  Q3 = NPN-Transistor [part_number=2N3904 package="TO92 [THT]"]
  Q4 = NPN-Transistor [part_number=2N3904 package="TO92 [THT]"]
  Q5 = Basic FET N-Channel [part_number=IRFZ44N package="TO220 [THT]"]
  Q6 = Basic FET N-Channel [part_number=IRFZ44N package="TO220 [THT]"]
  R4 = Resistor [tolerance=±1% resistance=1k package=THT]
  R5 = Resistor [tolerance=±1% resistance=1k package=THT]
  R6 = Resistor [tolerance=±1% resistance=1k package=THT]
  Raspberry_Pi_1 = Raspberry Pi 2
  LED2 = RGB LED - (4 legs) [package="5 mm [THT]"]
  R7 = Rotary Potentiometer (Small) [maximum_resistance=10kΩ package=THT]
  R8 = Rotary Potentiometer (Small) [maximum_resistance=10kΩ package=THT]
  R9 = Rotary Potentiometer (Small) [maximum_resistance=10kΩ package=THT]
  R10 = Resistor [tolerance=±1% resistance=100k package=THT]
  R11 = Resistor [tolerance=±1% resistance=100k package=THT]
  R12 = Resistor [tolerance=±1% resistance=100k package=THT]

nets:
  GND: Power_plug1.GND, Q1.source, Q5.source, Q6.source, Raspberry_Pi_1.GND, R10.Pin_1, R11.Pin_1, R12.Pin_1
  N1: Power_plug1.VCC, Q2.C, Q3.C, Q4.C, LED2.common_anode
  N2: Q1.gate, R6.Pin_1, R10.Pin_0
  N3: Q1.drain, LED2.red_cathode
  N4: Q2.E, R9.leg2
  N5: Q2.B, R2.Pin_1
  N6: R1.Pin_0, Raspberry_Pi_1.GPIO4
  N7: R1.Pin_1, Q3.B
  N8: R2.Pin_0, Raspberry_Pi_1.GPIO2
  N9: R3.Pin_0, Raspberry_Pi_1.GPIO3
  N10: R3.Pin_1, Q4.B
  N11: Q3.E, R7.leg2
  N12: Q4.E, R8.leg2
  N13: Q5.gate, R4.Pin_1, R12.Pin_0
  N14: Q5.drain, LED2.blue_cathode
  N15: Q6.gate, R5.Pin_1, R11.Pin_0
  N16: Q6.drain, LED2.green_cathode
  N17: R4.Pin_0, R7.wiper
  N18: R5.Pin_0, R8.wiper
  N19: R6.Pin_0, R9.wiper

notes:
  12V
  RGB Led strip
  RGB color value calibration
